// Logisim project 12_bit_ISA.circ as structural Verilog
module Register_File_4Bit (
  input  [7:0] Write_Data,
  input  [2:0] Read_Reg_1_RS,
  input  [2:0] Write_Reg_RD,
  input  RegWrite,
  input  [2:0] Read_Reg_2_RT,
  input  Clk,
  input  Clear,
  output [7:0] Read_Data_1,
  output [7:0] Read_Data_2
);

  wire and_1_out, and_2_out, and_3_out, and_4_out, and_5_out, and_6_out, and_7_out, and_8_out,
       decoder_1_out0, decoder_1_out1, decoder_1_out2, decoder_1_out3, decoder_1_out4, decoder_1_out5,
       decoder_1_out6, decoder_1_out7;
  wire [7:0] R0_q, R1_q, R2_q, R3_q, R4_q, R5_q, R6_q, R7_q;

  Decoder #(.select(3)) decoder_1 (
    .out0(decoder_1_out0), .out1(decoder_1_out1), .out2(decoder_1_out2), .out3(decoder_1_out3),
    .out4(decoder_1_out4), .out5(decoder_1_out5), .out6(decoder_1_out6), .out7(decoder_1_out7),
    .sel(Write_Reg_RD));  // open: en
  and and_1 (and_1_out, decoder_1_out0, RegWrite);
  and and_2 (and_2_out, decoder_1_out1, RegWrite);
  and and_3 (and_3_out, decoder_1_out2, RegWrite);
  and and_4 (and_4_out, decoder_1_out3, RegWrite);
  and and_5 (and_5_out, decoder_1_out4, RegWrite);
  and and_6 (and_6_out, decoder_1_out5, RegWrite);
  and and_7 (and_7_out, decoder_1_out6, RegWrite);
  and and_8 (and_8_out, decoder_1_out7, RegWrite);
  Register R0 (.en(and_1_out), .Q(R0_q), .clk(Clk), .clr(Clear));  // open: D
  Register R1 (.D(Write_Data), .en(and_2_out), .Q(R1_q), .clk(Clk), .clr(Clear));
  Register R2 (.D(Write_Data), .en(and_3_out), .Q(R2_q), .clk(Clk), .clr(Clear));
  Register R3 (.D(Write_Data), .en(and_4_out), .Q(R3_q), .clk(Clk), .clr(Clear));
  Register R4 (.D(Write_Data), .en(and_5_out), .Q(R4_q), .clk(Clk), .clr(Clear));
  Register R5 (.D(Write_Data), .en(and_6_out), .Q(R5_q), .clk(Clk), .clr(Clear));
  Register R6 (.D(Write_Data), .en(and_7_out), .Q(R6_q), .clk(Clk), .clr(Clear));
  Register R7 (.D(Write_Data), .en(and_8_out), .Q(R7_q), .clk(Clk), .clr(Clear));
  Multiplexer #(.select(3), .width(8)) multiplexer_1 (
    .in0(R0_q), .in1(R1_q), .in2(R2_q), .in3(R3_q), .in4(R4_q), .in5(R5_q), .in6(R6_q), .in7(R7_q),
    .out(Read_Data_1), .sel(Read_Reg_1_RS));  // open: en
  Multiplexer #(.select(3), .width(8)) multiplexer_2 (
    .in0(R0_q), .in1(R1_q), .in2(R2_q), .in3(R3_q), .in4(R4_q), .in5(R5_q), .in6(R6_q), .in7(R7_q),
    .out(Read_Data_2), .sel(Read_Reg_2_RT));  // open: en
endmodule

module _1_bit_ALU_Design (
  input  Cin,
  input  A,
  input  B,
  input  [1:0] Opcode,
  output Result,
  output Cout
);

  wire adder_1_out, and_1_out, and_2_out, multiplexer_1_out, not_1_out, or_1_out;

  and and_1 (and_1_out, A, B);
  or or_1 (or_1_out, A, B);
  not not_1 (not_1_out, B);
  Multiplexer multiplexer_1 (.in0(B), .in1(not_1_out), .out(multiplexer_1_out), .sel(and_2_out));  // open: en
  and and_2 (and_2_out, Opcode[0], Opcode[1]);
  Adder #(.width(1)) adder_1 (.a(A), .b(multiplexer_1_out), .out(adder_1_out), .cin(Cin), .cout(Cout));
  Multiplexer #(.select(2)) multiplexer_2 (
    .in0(and_1_out), .in1(or_1_out), .in2(adder_1_out), .in3(adder_1_out), .out(Result), .sel(Opcode));  // open: en
endmodule

module _16_bit_ALU_Design (
  input  [7:0] A,
  input  [7:0] B,
  input  [1:0] Opcode,
  input  Cin,
  output [7:0] Result,
  output Zero_signal,
  output C_out
);

  wire n1_bit_alu_design_1_cout, n1_bit_alu_design_2_cout, n1_bit_alu_design_3_cout,
       n1_bit_alu_design_4_cout, n1_bit_alu_design_5_cout, n1_bit_alu_design_6_cout, n1_bit_alu_design_7_cout;

  _1_bit_ALU_Design u_1_bit_alu_design_1 (
    .A(A[0]), .B(B[0]), .Result(Result[0]), .Cin(Cin), .Cout(n1_bit_alu_design_1_cout), .Opcode(Opcode));
  _1_bit_ALU_Design u_1_bit_alu_design_2 (
    .A(A[1]), .B(B[1]), .Result(Result[1]), .Cin(n1_bit_alu_design_1_cout), .Cout(n1_bit_alu_design_2_cout),
    .Opcode(Opcode));
  _1_bit_ALU_Design u_1_bit_alu_design_3 (
    .A(A[2]), .B(B[2]), .Result(Result[2]), .Cin(n1_bit_alu_design_2_cout), .Cout(n1_bit_alu_design_3_cout),
    .Opcode(Opcode));
  _1_bit_ALU_Design u_1_bit_alu_design_4 (
    .A(A[3]), .B(B[3]), .Result(Result[3]), .Cin(n1_bit_alu_design_3_cout), .Cout(n1_bit_alu_design_4_cout),
    .Opcode(Opcode));
  _1_bit_ALU_Design u_1_bit_alu_design_5 (
    .A(A[4]), .B(B[4]), .Result(Result[4]), .Cin(n1_bit_alu_design_4_cout), .Cout(n1_bit_alu_design_5_cout),
    .Opcode(Opcode));
  _1_bit_ALU_Design u_1_bit_alu_design_6 (
    .A(A[5]), .B(B[5]), .Result(Result[5]), .Cin(n1_bit_alu_design_5_cout), .Cout(n1_bit_alu_design_6_cout),
    .Opcode(Opcode));
  _1_bit_ALU_Design u_1_bit_alu_design_7 (
    .A(A[6]), .B(B[6]), .Result(Result[6]), .Cin(n1_bit_alu_design_6_cout), .Cout(n1_bit_alu_design_7_cout),
    .Opcode(Opcode));
  _1_bit_ALU_Design u_1_bit_alu_design_8 (
    .A(A[7]), .B(B[7]), .Result(Result[7]), .Cin(n1_bit_alu_design_7_cout), .Cout(C_out), .Opcode(Opcode));
  nor nor_1 (Zero_signal, Result[0], Result[1], Result[2], Result[3], Result[4], Result[5], Result[6], Result[7]);
endmodule

module Instruction_fetch_unit (
  input  clock,
  input  clear,
  output [15:0] Output
);

  wire [1:0] adder_1_out, register_1_q;

  Register #(.width(2)) register_1 (.D(adder_1_out), .Q(register_1_q), .clk(clock), .clr(clear));  // open: en
  ROM #(.addrWidth(2), .dataWidth(16)) rom_1 (.addr(register_1_q), .data(Output));  // open: sel
  Adder #(.width(2)) adder_1 (.a(register_1_q), .b(2'b01), .out(adder_1_out));  // open: cin, cout

  // Notes on the sheet:
  //   4 instructions and data bit 16
  //   contents of rom_1 (hex, n*v repeats v):
  //   2013 2458 3a3b
  //   Name: Aziza Zaman Sadia
  //   ID: 2231603642
  //   Group:01
  //   Course & Section: CSE332.11L
endmodule

module r_type_datapath (
  input  RegWrite,
  input  Clear,
  input  Clock,
  input  C_in,
  output [1:0] out_5,
  output [7:0] out_6,
  output [7:0] out_7,
  output [7:0] out_8,
  output out_9,
  output out_10
);

  wire [1:0] adder_1_out, register_1_q;
  wire [11:0] rom_1_data;

  Register #(.width(2)) register_1 (.D(adder_1_out), .Q(register_1_q), .clk(Clock), .clr(Clear));  // open: en
  Adder #(.width(2)) adder_1 (.a(register_1_q), .b(2'b01), .out(adder_1_out));  // open: cin, cout
  ROM #(.addrWidth(2), .dataWidth(12)) rom_1 (.addr(register_1_q), .data(rom_1_data));  // open: sel
  Bit_Extender #(.in_width(3), .out_width(2)) bit_extender_1 (.in(rom_1_data[11:9]), .out(out_5));
  Register_File_4Bit register_file_4bit_1 (
    .Write_Data(out_6), .Read_Data_1(out_7), .Read_Reg_1_RS(rom_1_data[8:6]), .Write_Reg_RD(rom_1_data[2:0]),
    .RegWrite(RegWrite), .Read_Data_2(out_8), .Clk(Clock), .Read_Reg_2_RT(rom_1_data[5:3]), .Clear(Clear));
  _16_bit_ALU_Design u_16_bit_alu_design_1 (
    .Result(out_6), .Zero_signal(out_9), .C_out(out_10), .A(out_7), .B(out_8), .Cin(C_in), .Opcode(out_5));

  // Notes on the sheet:
  //   contents of rom_1 (hex, n*v repeats v):
  //   3 58 3b
endmodule

module i_type_datapath (
  input  RegWrite,
  input  C_in,
  input  mem_write,
  input  mem_read,
  input  Clear,
  output [1:0] out_6,
  output [15:0] out_7,
  output [15:0] out_8,
  output out_9,
  output out_10,
  output [15:0] out_11
);

  wire Clock_out;
  wire [1:0] adder_1_out, bit_extender_3_out, register_1_q;
  wire [15:0] n16_bit_alu_design_1_p5, register_file_4bit_1_p9, rom_1_data;

  Button Clock (.out(Clock_out));
  Register #(.width(2)) register_1 (.D(adder_1_out), .Q(register_1_q), .clk(Clock_out), .clr(Clear));  // open: en
  Adder #(.width(2)) adder_1 (.a(register_1_q), .b(2'b01), .out(adder_1_out));  // open: cin, cout
  ROM #(.addrWidth(2), .dataWidth(16)) rom_1 (.addr(register_1_q), .data(rom_1_data));  // open: sel
  assign out_7 = {{12{1'b0}}, rom_1_data[3:0]};  // Bit_Extender bit_extender_1
  Bit_Extender #(.in_width(4), .out_width(2)) bit_extender_2 (.in(rom_1_data[15:12]), .out(out_6));
  // Register_File_4Bit register_file_4bit_1: pin names not known; wires that end beside it: out_11, RegWrite, Clock_out, Clear, rom_1_data[7:4], rom_1_data[11:8], rom_1_data[7:4], out_8, register_file_4bit_1_p9
  // _16_bit_ALU_Design 16_bit_alu_design_1: pin names not known; wires that end beside it: out_7, out_8, out_6, C_in, n16_bit_alu_design_1_p5, out_9, out_10
  Bit_Extender #(.in_width(16), .out_width(2)) bit_extender_3 (.in(n16_bit_alu_design_1_p5), .out(bit_extender_3_out));
  RAM #(.addrWidth(2), .dataWidth(16), .bus("separate")) ram_1 (
    .addr(bit_extender_3_out), .din(register_file_4bit_1_p9), .data(out_11), .str(mem_write),
    .clk(Clock_out), .ld(mem_read), .clr(Clear));  // open: sel

  // Notes on the sheet:
  //   contents of rom_1 (hex, n*v repeats v):
  //   2101 2123 2011 2010
endmodule
