// Logisim project logic_unit_with_ics.circ as structural Verilog: 1 circuit, main circuit main
module main (
  input  A1,
  input  A0,
  input  B1,
  input  B0,
  input  S1,
  input  S0,
  output F1,
  output F0
);

  wire n7404_1_pin2, n7404_1_pin4, n7408_1_pin3, n7408_1_pin6, n7432_1_pin3, n7432_1_pin6, n7486_1_pin3,
       n7486_1_pin6, n74153_1_pin1;

  _7408 #(.ShowInternalStructure("true")) u_7408_1 (
    .pin1(A1), .pin2(B1), .pin3(n7408_1_pin3), .pin4(A0), .pin5(B0), .pin6(n7408_1_pin6));  // open: pin13, pin12, pin11, pin10, pin9, pin8
  _7432 #(.ShowInternalStructure("true")) u_7432_1 (
    .pin1(A1), .pin2(B1), .pin3(n7432_1_pin3), .pin4(A0), .pin5(B0), .pin6(n7432_1_pin6));  // open: pin13, pin12, pin11, pin10, pin9, pin8
  _7486 #(.ShowInternalStructure("true")) u_7486_1 (
    .pin1(A1), .pin2(B1), .pin3(n7486_1_pin3), .pin4(A0), .pin5(B0), .pin6(n7486_1_pin6));  // open: pin13, pin12, pin11, pin10, pin9, pin8
  _7404 #(.ShowInternalStructure("true")) u_7404_1 (
    .pin1(A1), .pin2(n7404_1_pin2), .pin3(A0), .pin4(n7404_1_pin4));  // open: pin5, pin6, pin13, pin12, pin11, pin10, pin9, pin8
  _74153 #(.ShowInternalStructure("true")) u_74153_1 (
    .pin1(n74153_1_pin1), .pin2(S1), .pin3(n7404_1_pin2), .pin4(n7486_1_pin3), .pin5(n7432_1_pin3),
    .pin6(n7408_1_pin3), .pin7(F1), .pin15(n74153_1_pin1), .pin14(S0), .pin13(n7404_1_pin4),
    .pin12(n7486_1_pin6), .pin11(n7432_1_pin6), .pin10(n7408_1_pin6), .pin9(F0));
  // also tied to GND on the sheet: n74153_1_pin1

  // Notes on the sheet:
  //   A1B1
  //   A0B0
  //   Group: 01
  //   Name: Aziza Zaman Sadia
  //   ID: 2231603642
  //   Course &Section: CSE332.11
endmodule
