// Logisim project Lab_02_using_IC.circ as structural Verilog: 1 circuit, main circuit main
module main (
  input  S1,
  input  S0,
  input  Cin,
  input  A1,
  input  A0,
  input  B1,
  input  B0,
  output D1,
  output D0,
  output Cout
);

  wire n7404_1_pin2, n7404_1_pin4, n74153_1_pin1, n74153_1_pin3, n74153_1_pin4, n74153_1_pin7, n74153_1_pin9;

  _7404 #(.ShowInternalStructure("true")) u_7404_1 (
    .pin1(B0), .pin2(n7404_1_pin2), .pin3(B1), .pin4(n7404_1_pin4));  // open: pin5, pin6, pin13, pin12, pin11, pin10, pin9, pin8
  _74153 #(.ShowInternalStructure("true")) u_74153_1 (
    .pin1(n74153_1_pin1), .pin2(S1), .pin3(n74153_1_pin3), .pin4(n74153_1_pin4), .pin5(n7404_1_pin2),
    .pin6(B0), .pin7(n74153_1_pin7), .pin15(n74153_1_pin1), .pin14(S0), .pin13(n74153_1_pin3),
    .pin12(n74153_1_pin4), .pin11(n7404_1_pin4), .pin10(B1), .pin9(n74153_1_pin9));
  _74283 #(.ShowInternalStructure("true")) u_74283_1 (
    .pin1(D1), .pin2(n74153_1_pin9), .pin3(A1), .pin4(D0), .pin5(A0), .pin6(n74153_1_pin7), .pin7(Cin),
    .pin13(Cout));  // open: pin15, pin14, pin12, pin11, pin10, pin9
  // also tied to GND on the sheet: {n74153_1_pin4, n74153_1_pin1}
  // also tied to VCC on the sheet: n74153_1_pin3

  // Notes on the sheet:
  //   ID: 2231603642
  //   Name: Aziza Zaman Sadia
  //   Course & Section: CSE332.11
endmodule
