// Logisim project Lab_2_arithmetic_unit.circ as structural Verilog: 1 circuit, main circuit main
module main (
  input  A1,
  input  A0,
  input  B1,
  input  B0,
  input  Cin,
  input  [1:0] S1S0,
  output D1,
  output D0,
  output Cout
);

  wire adder_1_cout, multiplexer_1_out, multiplexer_2_out, not_1_out, not_2_out;

  not not_1 (not_1_out, B1);
  not not_2 (not_2_out, B0);
  Multiplexer #(.select(2)) multiplexer_1 (
    .in0(B0), .in1(not_2_out), .in2(1'b0), .in3(1'b1), .out(multiplexer_1_out), .sel(S1S0));
  Multiplexer #(.select(2)) multiplexer_2 (
    .in0(B1), .in1(not_1_out), .in2(1'b0), .in3(1'b1), .out(multiplexer_2_out), .sel(S1S0));
  Adder #(.width(1)) adder_1 (.a(multiplexer_1_out), .b(A0), .out(D0), .cin(Cin), .cout(adder_1_cout));
  Adder #(.width(1)) adder_2 (.a(multiplexer_2_out), .b(A1), .out(D1), .cin(adder_1_cout), .cout(Cout));

  // Notes on the sheet:
  //   Group: 01
  //   Name: Aziza Zaman Sadia 
  //   ID: 2231603642
  //   Course &Section: CSE332.11
endmodule
