// Logisim project Lab_03_multiplication_using_basic_gates.circ as structural Verilog: 1 circuit, main circuit main
module main (
  input  Constant_0,
  input  A3,
  input  A2,
  input  A1,
  input  B3,
  input  B2,
  input  B1,
  output [5:0] S
);

  wire [1:0] A1B2_out;
  wire [2:0] A2B1_out, A3B1_out;
  wire [2:1] adder_1_out;
  wire [2:2] adder_1_cout;

  and A1B1 (S[0], A1, B1);
  and A1B2 (A1B2_out[0], A1, B2);
  and A1B3 (A1B2_out[1], A1, B3);
  and A2B1 (A2B1_out[0], A2, B1);
  and A2B2 (A2B1_out[1], A2, B2);
  and A2B3 (A2B1_out[2], A2, B3);
  and A3B1 (A3B1_out[0], A3, B1);
  and A3B2 (A3B1_out[1], A3, B2);
  and A3B3 (A3B1_out[2], A3, B3);
  Adder #(.width(3)) adder_1 (
    .a({Constant_0, A1B2_out}), .b(A2B1_out), .out({adder_1_out, S[1]}), .cin(Constant_0),
    .cout(adder_1_cout[2]));
  Adder #(.width(3)) adder_2 (
    .a(A3B1_out), .b({adder_1_cout[2], adder_1_out}), .out(S[4:2]), .cin(Constant_0), .cout(S[5]));

  // Notes on the sheet:
  //   ID: 2231603642
  //   Group:01
  //   Name: Aziza Zaman Sadia
  //   Course & Section: CSE332.11
endmodule
