// Logisim project three_bit_Up_down_Counter.circ as structural Verilog: 1 circuit, main circuit main
module main (
  input  M,
  input  S,
  output Qc,
  output Qb,
  output Qa
);

  wire and_1_out, and_2_out, Clk_out, d_ff_2_qn, d_ff_3_qn, not_1_out, or_1_out, xor_1_out, xor_2_out,
       xor_3_out, xor_4_out;

  not not_1 (not_1_out, M);
  and and_1 (and_1_out, not_1_out, Qa, Qb);
  Clock Clk (.out(Clk_out));
  or or_1 (or_1_out, and_1_out, and_2_out);
  and and_2 (and_2_out, M, d_ff_2_qn, d_ff_3_qn);
  xor xor_1 (xor_1_out, Qc, or_1_out);
  D_Flip_Flop d_ff_1 (.D(xor_1_out), .clk(Clk_out), .Q(Qc), .reset(S));  // open: Qn, preset
  xor xor_2 (xor_2_out, M, Qa);
  D_Flip_Flop d_ff_2 (.D(xor_3_out), .clk(Clk_out), .Q(Qb), .Qn(d_ff_2_qn), .reset(S));  // open: preset
  xor xor_3 (xor_3_out, Qb, xor_2_out);
  D_Flip_Flop d_ff_3 (.D(xor_4_out), .clk(Clk_out), .Q(Qa), .Qn(d_ff_3_qn), .reset(S));  // open: preset
  xor xor_4 (xor_4_out, Qa, 1'b1);

  // Notes on the sheet:
  //   M'QaQb
  //   MQa'Qb'
  //   Qc
  //   Name: Aziza Zaman Sadia
  //   ID: 2231603642
  //   Group: 01
  //   Course & Section: CSE332.11
  //   Qb
  //   Qb'
  //   Qa
  //   Qa'
endmodule
