// Logisim project two_bit_Up_down_Counter.circ as structural Verilog: 1 circuit, main circuit main
module main (
  input  _4,
  output out_2,
  output out_3
);

  wire clock_1_out, xor_1_out, xor_2_out, xor_3_out;

  Clock clock_1 (.out(clock_1_out));
  xor xor_1 (xor_1_out, _4, out_3);
  xor xor_2 (xor_2_out, out_2, xor_1_out);
  D_Flip_Flop d_ff_1 (.D(xor_2_out), .clk(clock_1_out), .Q(out_2));  // open: Qn, preset, reset
  xor xor_3 (xor_3_out, out_3, 1'b1);
  D_Flip_Flop d_ff_2 (.D(xor_3_out), .clk(clock_1_out), .Q(out_3));  // open: Qn, preset, reset

  // Notes on the sheet:
  //   6
  //   5
  //   9
  //   10
  //   8
  //   12
  //   11
  //   9
  //   1
  //   2
  //   3
  //   2
  //   5
  //   3
endmodule
