// Logisim project Lab_05_4_Bit_Register_File.circ as structural Verilog
module Register_File_4Bit (
  input  [15:0] Write_Data,
  input  [3:0] Read_Reg_1_RS,
  input  [3:0] Write_Reg_RD,
  input  RegWrite,
  input  Clk,
  input  [3:0] Read_Reg_2_RT,
  input  Clear,
  output [15:0] Read_Data_1,
  output [15:0] Read_Data_2
);

  wire and_1_out, and_2_out, and_3_out, and_4_out, and_5_out, and_6_out, and_7_out, and_8_out, and_9_out,
       and_10_out, and_11_out, and_12_out, and_13_out, and_14_out, and_15_out, and_16_out, decoder_1_out0,
       decoder_1_out1, decoder_1_out2, decoder_1_out3, decoder_1_out4, decoder_1_out5, decoder_1_out6,
       decoder_1_out7, decoder_1_out8, decoder_1_out9, decoder_1_out10, decoder_1_out11, decoder_1_out12,
       decoder_1_out13, decoder_1_out14, decoder_1_out15;
  wire [15:0] R1_q, R2_q, R3_q, R4_q, R5_q, R6_q, R7_q, R8_q, R9_q, R10_q, R11_q, R12_q, R13_q, R14_q, R15_q,
       R16_q;

  Decoder #(.select(4)) decoder_1 (
    .out0(decoder_1_out0), .out1(decoder_1_out1), .out2(decoder_1_out2), .out3(decoder_1_out3),
    .out4(decoder_1_out4), .out5(decoder_1_out5), .out6(decoder_1_out6), .out7(decoder_1_out7),
    .out8(decoder_1_out8), .out9(decoder_1_out9), .out10(decoder_1_out10), .out11(decoder_1_out11),
    .out12(decoder_1_out12), .out13(decoder_1_out13), .out14(decoder_1_out14), .out15(decoder_1_out15),
    .sel(Write_Reg_RD));  // open: en
  and and_1 (and_1_out, decoder_1_out0, RegWrite);
  and and_2 (and_2_out, decoder_1_out1, RegWrite);
  and and_3 (and_3_out, decoder_1_out2, RegWrite);
  and and_4 (and_4_out, decoder_1_out3, RegWrite);
  and and_5 (and_5_out, decoder_1_out4, RegWrite);
  and and_6 (and_6_out, decoder_1_out5, RegWrite);
  and and_7 (and_7_out, decoder_1_out6, RegWrite);
  and and_8 (and_8_out, decoder_1_out7, RegWrite);
  and and_9 (and_9_out, decoder_1_out8, RegWrite);
  and and_10 (and_10_out, decoder_1_out9, RegWrite);
  and and_11 (and_11_out, decoder_1_out10, RegWrite);
  and and_12 (and_12_out, decoder_1_out11, RegWrite);
  and and_13 (and_13_out, decoder_1_out12, RegWrite);
  and and_14 (and_14_out, decoder_1_out13, RegWrite);
  and and_15 (and_15_out, decoder_1_out14, RegWrite);
  and and_16 (and_16_out, decoder_1_out15, RegWrite);
  Register #(.width(16)) R1 (.D(Write_Data), .en(and_1_out), .Q(R1_q), .clk(Clk), .clr(Clear));
  Register #(.width(16)) R5 (.D(Write_Data), .en(and_5_out), .Q(R5_q), .clk(Clk), .clr(Clear));
  Register #(.width(16)) R9 (.D(Write_Data), .en(and_9_out), .Q(R9_q), .clk(Clk), .clr(Clear));
  Register #(.width(16)) R13 (.D(Write_Data), .en(and_13_out), .Q(R13_q), .clk(Clk), .clr(Clear));
  Register #(.width(16)) R2 (.D(Write_Data), .en(and_2_out), .Q(R2_q), .clk(Clk), .clr(Clear));
  Register #(.width(16)) R6 (.D(Write_Data), .en(and_6_out), .Q(R6_q), .clk(Clk), .clr(Clear));
  Register #(.width(16)) R10 (.D(Write_Data), .en(and_10_out), .Q(R10_q), .clk(Clk), .clr(Clear));
  Register #(.width(16)) R14 (.D(Write_Data), .en(and_14_out), .Q(R14_q), .clk(Clk), .clr(Clear));
  Register #(.width(16)) R3 (.D(Write_Data), .en(and_3_out), .Q(R3_q), .clk(Clk), .clr(Clear));
  Register #(.width(16)) R7 (.D(Write_Data), .en(and_7_out), .Q(R7_q), .clk(Clk), .clr(Clear));
  Register #(.width(16)) R11 (.D(Write_Data), .en(and_11_out), .Q(R11_q), .clk(Clk), .clr(Clear));
  Register #(.width(16)) R15 (.D(Write_Data), .en(and_15_out), .Q(R15_q), .clk(Clk), .clr(Clear));
  Register #(.width(16)) R4 (.D(Write_Data), .en(and_4_out), .Q(R4_q), .clk(Clk), .clr(Clear));
  Register #(.width(16)) R8 (.D(Write_Data), .en(and_8_out), .Q(R8_q), .clk(Clk), .clr(Clear));
  Register #(.width(16)) R12 (.D(Write_Data), .en(and_12_out), .Q(R12_q), .clk(Clk), .clr(Clear));
  Register #(.width(16)) R16 (.D(Write_Data), .en(and_16_out), .Q(R16_q), .clk(Clk), .clr(Clear));
  Multiplexer #(.select(4), .width(16)) multiplexer_1 (
    .in0(R1_q), .in1(R2_q), .in2(R3_q), .in3(R4_q), .in4(R5_q), .in5(R6_q), .in6(R7_q), .in7(R8_q),
    .in8(R9_q), .in9(R10_q), .in10(R11_q), .in11(R12_q), .in12(R13_q), .in13(R14_q), .in14(R15_q),
    .in15(R16_q), .out(Read_Data_1), .sel(Read_Reg_1_RS));  // open: en
  Multiplexer #(.select(4), .width(16)) multiplexer_2 (
    .in0(R1_q), .in1(R2_q), .in2(R3_q), .in3(R4_q), .in4(R5_q), .in5(R6_q), .in6(R7_q), .in7(R8_q),
    .in8(R9_q), .in9(R10_q), .in10(R11_q), .in11(R12_q), .in12(R13_q), .in13(R14_q), .in14(R15_q),
    .in15(R16_q), .out(Read_Data_2), .sel(Read_Reg_2_RT));  // open: en

  // Notes on the sheet:
  //   Name: Aziza Zaman Sadia
  //   ID: 2231603642
  //   Group: 01
  //   Course & Section: CSE332.11L
endmodule

module _1_bit_ALU_Design (
  input  Cin,
  input  A,
  input  B,
  input  [1:0] Opcode,
  output Result,
  output Cout
);

  wire adder_1_out, and_1_out, and_2_out, multiplexer_1_out, not_1_out, or_1_out;

  and and_1 (and_1_out, A, B);
  or or_1 (or_1_out, A, B);
  not not_1 (not_1_out, B);
  Multiplexer multiplexer_1 (.in0(B), .in1(not_1_out), .out(multiplexer_1_out), .sel(and_2_out));  // open: en
  and and_2 (and_2_out, Opcode[0], Opcode[1]);
  Adder #(.width(1)) adder_1 (.a(A), .b(multiplexer_1_out), .out(adder_1_out), .cin(Cin), .cout(Cout));
  Multiplexer #(.select(2)) multiplexer_2 (
    .in0(and_1_out), .in1(or_1_out), .in2(adder_1_out), .in3(adder_1_out), .out(Result), .sel(Opcode));  // open: en
endmodule

module _16_bit_ALU_Design (
  input  [1:0] Opcode,
  input  C_in,
  input  [15:0] A,
  input  [15:0] B,
  output [15:0] Result,
  output Zero_signal,
  output C_out
);

  wire n1_bit_alu_design_1_cout, n1_bit_alu_design_2_cout, n1_bit_alu_design_3_cout,
       n1_bit_alu_design_4_cout, n1_bit_alu_design_9_cout, n1_bit_alu_design_10_cout,
       n1_bit_alu_design_11_cout, n1_bit_alu_design_12_cout, n1_bit_alu_design_13_cout,
       n1_bit_alu_design_14_cout, n1_bit_alu_design_15_cout, n1_bit_alu_design_16_cout,
       n1_bit_alu_design_17_cout, n1_bit_alu_design_18_cout, n1_bit_alu_design_19_cout;

  _1_bit_ALU_Design u_1_bit_alu_design_1 (
    .A(A[0]), .B(B[0]), .Result(Result[0]), .Cin(C_in), .Cout(n1_bit_alu_design_1_cout), .Opcode(Opcode));
  _1_bit_ALU_Design u_1_bit_alu_design_2 (
    .A(A[1]), .B(B[1]), .Result(Result[1]), .Cin(n1_bit_alu_design_1_cout), .Cout(n1_bit_alu_design_2_cout),
    .Opcode(Opcode));
  _1_bit_ALU_Design u_1_bit_alu_design_3 (
    .A(A[3]), .B(B[2]), .Result(Result[2]), .Cin(n1_bit_alu_design_2_cout), .Cout(n1_bit_alu_design_3_cout),
    .Opcode(Opcode));
  _1_bit_ALU_Design u_1_bit_alu_design_4 (
    .A(A[2]), .B(B[3]), .Result(Result[3]), .Cin(n1_bit_alu_design_3_cout), .Cout(n1_bit_alu_design_4_cout),
    .Opcode(Opcode));
  _1_bit_ALU_Design u_1_bit_alu_design_5 ();  // open: A, B, Result, Cin, Cout, Opcode
  _1_bit_ALU_Design u_1_bit_alu_design_6 ();  // open: A, B, Result, Cin, Cout, Opcode
  _1_bit_ALU_Design u_1_bit_alu_design_7 ();  // open: A, B, Result, Cin, Cout, Opcode
  _1_bit_ALU_Design u_1_bit_alu_design_8 ();  // open: A, B, Result, Cin, Cout, Opcode
  _1_bit_ALU_Design u_1_bit_alu_design_9 (
    .A(A[4]), .B(B[4]), .Result(Result[4]), .Cin(n1_bit_alu_design_4_cout), .Cout(n1_bit_alu_design_9_cout),
    .Opcode(Opcode));
  _1_bit_ALU_Design u_1_bit_alu_design_10 (
    .A(A[5]), .B(B[5]), .Result(Result[5]), .Cin(n1_bit_alu_design_9_cout), .Cout(n1_bit_alu_design_10_cout),
    .Opcode(Opcode));
  _1_bit_ALU_Design u_1_bit_alu_design_11 (
    .A(A[6]), .B(B[6]), .Result(Result[6]), .Cin(n1_bit_alu_design_10_cout),
    .Cout(n1_bit_alu_design_11_cout), .Opcode(Opcode));
  _1_bit_ALU_Design u_1_bit_alu_design_12 (
    .A(A[7]), .B(B[7]), .Result(Result[7]), .Cin(n1_bit_alu_design_11_cout),
    .Cout(n1_bit_alu_design_12_cout), .Opcode(Opcode));
  _1_bit_ALU_Design u_1_bit_alu_design_13 (
    .A(A[8]), .B(B[8]), .Result(Result[8]), .Cin(n1_bit_alu_design_12_cout),
    .Cout(n1_bit_alu_design_13_cout), .Opcode(Opcode));
  _1_bit_ALU_Design u_1_bit_alu_design_14 (
    .A(A[9]), .B(B[9]), .Result(Result[9]), .Cin(n1_bit_alu_design_13_cout),
    .Cout(n1_bit_alu_design_14_cout), .Opcode(Opcode));
  _1_bit_ALU_Design u_1_bit_alu_design_15 (
    .A(A[10]), .B(B[10]), .Result(Result[10]), .Cin(n1_bit_alu_design_14_cout),
    .Cout(n1_bit_alu_design_15_cout), .Opcode(Opcode));
  _1_bit_ALU_Design u_1_bit_alu_design_16 (
    .A(A[11]), .B(B[11]), .Result(Result[11]), .Cin(n1_bit_alu_design_15_cout),
    .Cout(n1_bit_alu_design_16_cout), .Opcode(Opcode));
  _1_bit_ALU_Design u_1_bit_alu_design_17 (
    .A(A[12]), .B(B[12]), .Result(Result[12]), .Cin(n1_bit_alu_design_16_cout),
    .Cout(n1_bit_alu_design_17_cout), .Opcode(Opcode));
  _1_bit_ALU_Design u_1_bit_alu_design_18 (
    .A(A[13]), .B(B[13]), .Result(Result[13]), .Cin(n1_bit_alu_design_17_cout),
    .Cout(n1_bit_alu_design_18_cout), .Opcode(Opcode));
  _1_bit_ALU_Design u_1_bit_alu_design_19 (
    .A(A[14]), .B(B[14]), .Result(Result[14]), .Cin(n1_bit_alu_design_18_cout),
    .Cout(n1_bit_alu_design_19_cout), .Opcode(Opcode));
  _1_bit_ALU_Design u_1_bit_alu_design_20 (
    .A(A[15]), .B(B[15]), .Result(Result[15]), .Cin(n1_bit_alu_design_19_cout), .Cout(C_out), .Opcode(Opcode));
  nor nor_1 (Zero_signal, Result[0], Result[1], Result[2], Result[3], Result[4], Result[5], Result[6], Result[7], Result[8], Result[9], Result[10], Result[11], Result[12], Result[13], Result[14], Result[15]);

  // Notes on the sheet:
  //   Group: 01
  //   Name: Aziza Zaman Sadia
  //   ID: 2231603642
  //   Course & Section : CSE332.11L
endmodule
